# Fritzing sketch schakeling (saved by Fritzing 0.8.7b)
breadboards: 1

parts:
  Raspberry_Pi_1 = Raspberry Pi 3
  IC2 = L293D [package=THT]
  M2 = DC Motor
  VCC2 = Battery block 9V
  J2 = Basic Servo
  LED1 = LEDs [package=led10mm]
  LED2 = LEDs [package=led10mm]
  R1 = Resistor [tolerance=±5% resistance=220 package="0603 [SMD]"]

nets:
  N1: Raspberry_Pi_1.3v3, IC2.+V
  N2: Raspberry_Pi_1.GPIO2, IC2.In_1
  N3: Raspberry_Pi_1.GPIO3, IC2.In_2
  N4: Raspberry_Pi_1.GIPO4, IC2.Enable_1
  N5: Raspberry_Pi_1.GIPO27, LED1.C, LED2.C
  GND: Raspberry_Pi_1.GND, IC2.0V, VCC2.-, J2.gnd, R1.Pin_0
  N6: IC2.Out_1_(_Controlled_by_Enable_1_), M2.pin_2
  N7: IC2.Out_2_(_Controlled_by_Enable_1_), M2.pin_1
  N8: IC2.+Vmotor, VCC2.+
  N9: LED1.A, LED2.A, R1.Pin_1
