# Fritzing sketch schakeling_pot (saved by Fritzing 0.8.7b)
breadboards: 2

parts:
  Raspberry_Pi_1 = Raspberry Pi 3
  IC2 = L293D [package=THT]
  M2 = DC Motor
  VCC2 = Battery block 9V
  J2 = Basic Servo
  LED1 = LEDs [package=led10mm]
  LED2 = LEDs [package=led10mm]
  R1 = Resistor [tolerance=±5% resistance=220 package="0603 [SMD]"]
  IC3 = MCP3008 8-channel 10-bit ADC [part_number=MCP3008]
  U1 = POT [package=pot_alpha_rv16af-20]

nets:
  3V3: Raspberry_Pi_1.3v3, Raspberry_Pi_1.3V3, IC2.+V, IC3.no_name_yet#15, IC3.no_name_yet#16, U1.A
  N1: Raspberry_Pi_1.GPIO2, IC2.In_1
  N2: Raspberry_Pi_1.GPIO3, IC2.In_2
  N3: Raspberry_Pi_1.GIPO4, IC2.Enable_1
  N4: Raspberry_Pi_1.GIPO27, LED1.C, LED2.C
  N5: Raspberry_Pi_1.GIPO19, IC3.no_name_yet#12
  GND: Raspberry_Pi_1.GND, IC2.0V, VCC2.-, J2.gnd, R1.Pin_0, IC3.no_name_yet#14, U1.E
  N6: Raspberry_Pi_1.GIPO20, IC3.no_name_yet#11
  N7: Raspberry_Pi_1.GIPO16, IC3.no_name_yet#13
  N8: Raspberry_Pi_1.GIPO25, IC3.no_name_yet#10
  N9: IC2.Out_1_(_Controlled_by_Enable_1_), M2.pin_2
  N10: IC2.Out_2_(_Controlled_by_Enable_1_), M2.pin_1
  N11: IC2.+Vmotor, VCC2.+
  N12: LED1.A, LED2.A, R1.Pin_1
  N13: IC3.MCP_3008, U1.S
